# Fritzing sketch sketch (saved by Fritzing 0.9.3b)
breadboards: 1

parts:
  Part1 = Arduino Uno (Rev3)
  part = 7 Segment Display
  S1 = Pushbutton [package="[SMD]"]
  S2 = Pushbutton [package="[SMD]"]
  M1 = DC Motor
  R1 = Resistor [tolerance=±5% resistance=100 package="1206 [SMD]"]
  R2 = Resistor [tolerance=±5% resistance=5k package="1206 [SMD]"]
  R3 = Resistor [tolerance=±5% resistance=100k package="1206 [SMD]"]
  R4 = Resistor [tolerance=±5% resistance=1k package=THT]
  D1 = Rectifier Diode [package="Melf DO-213 AA [SMD]"]
  Q1 = NPN-Transistor [package="SOT-23 [SMD]"]
  R5 = Resistor [tolerance=±5% resistance=330 package=THT]

nets:
  N1: Part1.A0, S1.Pin_3, S1.Pin_4, S2.Pin_3, S2.Pin_4, R3.Pin_0
  N2: Part1.D9_PWM, R5.Pin_1
  N3: Part1.GND, R3.Pin_1, R4.Pin_1, Q1.1
  N4: Part1.D1/TX, part.Segment_C
  N5: Part1.D2, part.Segment_D
  N6: Part1.D3_PWM, part.Segment_E
  N7: Part1.D4, part.Segment_B
  N8: Part1.D5_PWM, part.Segment_A
  N9: Part1.D6_PWM, part.Segment_F
  N10: Part1.D7, part.Segment_G
  N11: Part1.5V, M1.pin_1, R1.Pin_1, R2.Pin_1, D1.cathode
  N12: part.common_anode, R4.Pin_0
  N13: S1.Pin_1, S1.Pin_2, R1.Pin_0
  N14: S2.Pin_1, S2.Pin_2, R2.Pin_0
  N15: M1.pin_2, D1.anode, Q1.2
  N16: Q1.0, R5.Pin_0
